// Logisim project CPU.circ as structural Verilog: 6 circuits, main circuit main
module main (
  input  A,
  input  B,
  output out_3,
  output out_4
);

  xor xor_1 (out_3, A, B);
  and and_1 (out_4, A, B);
endmodule

module Full_Adder (
  input  A,
  input  B,
  input  Cin,
  output Sum,
  output Cout
);

  wire and_1_out, and_2_out, xor_1_out;

  xor xor_1 (xor_1_out, A, B);
  xor xor_2 (Sum, xor_1_out, Cin);
  and and_1 (and_1_out, Cin, xor_1_out);
  and and_2 (and_2_out, A, B);
  or or_1 (Cout, and_1_out, and_2_out);
endmodule

module Addwe8bit (
  input  B2,
  input  B1,
  input  A0,
  input  B0,
  input  A6,
  input  A2,
  input  A1,
  input  B3,
  input  A7,
  input  B4,
  input  B7,
  input  B5,
  input  B6,
  input  A3,
  input  A5,
  input  A4,
  input  Cin,
  output Cout,
  output S5,
  output S6,
  output S7,
  output S0,
  output S1,
  output S2,
  output S3,
  output S4
);

  wire full_adder_1_cout, full_adder_2_cout, full_adder_3_cout, full_adder_4_cout, full_adder_5_cout,
       full_adder_6_cout, full_adder_7_cout;

  Full_Adder full_adder_1 (.A(A0), .B(B0), .Cin(Cin), .Sum(S0), .Cout(full_adder_1_cout));
  Full_Adder full_adder_2 (.A(A1), .B(B1), .Cin(full_adder_1_cout), .Sum(S1), .Cout(full_adder_2_cout));
  Full_Adder full_adder_3 (.A(A2), .B(B2), .Cin(full_adder_2_cout), .Sum(S2), .Cout(full_adder_3_cout));
  Full_Adder full_adder_4 (.A(A3), .B(B3), .Cin(full_adder_3_cout), .Sum(S3), .Cout(full_adder_4_cout));
  Full_Adder full_adder_5 (.A(A4), .B(B4), .Cin(full_adder_4_cout), .Sum(S4), .Cout(full_adder_5_cout));
  Full_Adder full_adder_6 (.A(A5), .B(B5), .Cin(full_adder_5_cout), .Sum(S5), .Cout(full_adder_6_cout));
  Full_Adder full_adder_7 (.A(A6), .B(B6), .Cin(full_adder_6_cout), .Sum(S6), .Cout(full_adder_7_cout));
  Full_Adder full_adder_8 (.A(A7), .B(B7), .Cin(full_adder_7_cout), .Sum(S7), .Cout(Cout));
endmodule

module ALU (
  input  [7:0] A,
  input  [7:0] B,
  input  [2:0] Op,
  output out_4,
  output [7:0] Result
);

  wire [7:0] adder_1_out, and_1_out, not_1_out, or_1_out, shifter_1_out, shifter_2_out, subtractor_1_out,
       xor_1_out;

  Adder adder_1 (.a(A), .b(B), .out(adder_1_out), .cout(out_4));  // open: cin
  Subtractor subtractor_1 (.a(A), .b(B), .out(subtractor_1_out));  // open: bin, bout
  assign and_1_out = A & B;  // AND_Gate and_1, 8 bits wide
  assign xor_1_out = A ^ B;  // XOR_Gate xor_1, 8 bits wide
  assign or_1_out = A | B;  // OR_Gate or_1, 8 bits wide
  Shifter shifter_1 (.in(A), .\dist (3'b001), .out(shifter_1_out));
  Shifter #(.shift("lr")) shifter_2 (.in(A), .\dist (3'b001), .out(shifter_2_out));
  assign not_1_out = ~A;  // NOT_Gate not_1, 8 bits wide
  Multiplexer #(.select(3), .width(8)) multiplexer_1 (
    .in0(adder_1_out), .in1(subtractor_1_out), .in2(and_1_out), .in3(or_1_out), .in4(xor_1_out),
    .in5(not_1_out), .in6(shifter_1_out), .in7(shifter_2_out), .out(Result), .sel(Op));
  Hex_Digit_Display hex_digit_display_1 (.value(Result[7:4]));  // open: dp
  Hex_Digit_Display hex_digit_display_2 (.value(Result[3:0]));  // open: dp
endmodule

module Rigester8 (
  input  [7:0] D,
  input  Load,
  input  CLK,
  input  Reset,
  output [7:0] Q
);

  Register register_1 (.D(D), .en(Load), .clk(CLK), .Q(Q), .clr(Reset));
  Hex_Digit_Display hex_digit_display_1 (.value(Q[3:0]));  // open: dp
  Hex_Digit_Display hex_digit_display_2 (.value(Q[7:4]));  // open: dp
endmodule

module ProgramCounter (
  input  CLK,
  input  Reset,
  input  Inc,
  input  [7:0] D,
  input  Load,
  output [7:0] PC
);

  wire [7:0] adder_1_out, multiplexer_1_out, multiplexer_2_out;

  Register register_1 (.D(multiplexer_2_out), .en(1'b1), .clk(CLK), .Q(PC), .clr(Reset));
  Hex_Digit_Display hex_digit_display_1 (.value(PC[7:4]));  // open: dp
  Hex_Digit_Display hex_digit_display_2 (.value(PC[3:0]));  // open: dp
  Adder adder_1 (.a(PC), .b(8'h1), .out(adder_1_out));  // open: cin, cout
  Multiplexer #(.width(8)) multiplexer_1 (.in0(PC), .in1(adder_1_out), .out(multiplexer_1_out), .sel(Inc));
  Multiplexer #(.width(8)) multiplexer_2 (.in0(multiplexer_1_out), .in1(D), .out(multiplexer_2_out), .sel(Load));
endmodule
